# Fritzing sketch schema (saved by Fritzing 0.9.2b)
breadboards: 1

parts:
  Componente1 = Arduino Uno (Rev3)
  Componente2 = SRF05 Ultrasonic Rangefinder

nets:
  N1: Componente1.D8, Componente2.Echo
  N2: Componente1.D13/SCK, Componente2.Trig
  5V: Componente1.5V, Componente2.VCC
  GND: Componente1.GND, Componente2.GND
